// Logisim project CPUFinal11.circ as structural Verilog: 10 circuits, main circuit main
module main (
  input  in_1,
  output [15:0] out_2,
  output [7:0] out_3
);

  wire clk;
  wire [3:0] reg_file_1_out_a, reg_file_1_out_b;
  wire [15:0] register_1_q;

  Clock clock_1 (.out(clk));
  Counter counter_1 (.clk(clk), .Q(out_3));  // open: clr, load, up, count, D, carry
  ROM #(.dataWidth(16)) rom_1 (.addr(out_3), .data(out_2));
  Register #(.width(16)) register_1 (.D(out_2), .en(in_1), .clk(clk), .Q(register_1_q));  // open: clr
  REG_FILE reg_file_1 (.OUT_A(reg_file_1_out_a), .OUT_B(reg_file_1_out_b));  // open: CLK, Write, IN_VAL, Ra, Rd, Rb
  ALU alu_1 (.A(reg_file_1_out_a), .B(reg_file_1_out_b));  // open: Opcode, out_4, O, C, Z, N

  // Notes on the sheet:
  //   contents of rom_1 (hex, n*v repeats v):
  //   102 3355
endmodule

module ADDER_4 (
  input  [3:0] A,
  input  [3:0] B,
  input  Cin,
  output [3:0] Sum,
  output Overflow,
  output Carry
);

  wire adder_1_cout, adder_2_cout, adder_3_cout, subtractor_1_bout, subtractor_2_bout, subtractor_3_bout;
  wire [3:0] adder_1_out, subtractor_1_out;

  Adder #(.width(1)) adder_1 (.a(A[0]), .b(B[0]), .out(adder_1_out[0]), .cin(1'b0), .cout(adder_1_cout));
  Adder #(.width(1)) adder_2 (.a(A[1]), .b(B[1]), .out(adder_1_out[1]), .cin(adder_1_cout), .cout(adder_2_cout));
  Adder #(.width(1)) adder_3 (.a(A[2]), .b(B[2]), .out(adder_1_out[2]), .cin(adder_2_cout), .cout(adder_3_cout));
  Adder #(.width(1)) adder_4 (.a(A[3]), .b(B[3]), .out(adder_1_out[3]), .cin(adder_3_cout), .cout(Carry));
  Subtractor #(.width(1)) subtractor_1 (
    .a(A[0]), .b(B[0]), .out(subtractor_1_out[0]), .bin(1'b0), .bout(subtractor_1_bout));
  Subtractor #(.width(1)) subtractor_2 (
    .a(A[1]), .b(B[1]), .out(subtractor_1_out[1]), .bin(subtractor_1_bout), .bout(subtractor_2_bout));
  Subtractor #(.width(1)) subtractor_3 (
    .a(A[2]), .b(B[2]), .out(subtractor_1_out[2]), .bin(subtractor_2_bout), .bout(subtractor_3_bout));
  Subtractor #(.width(1)) subtractor_4 (
    .a(A[3]), .b(B[3]), .out(subtractor_1_out[3]), .bin(subtractor_3_bout));  // open: bout
  xor xor_1 (Overflow, adder_3_cout, Carry);
  Multiplexer #(.width(4)) multiplexer_1 (.in0(adder_1_out), .in1(subtractor_1_out), .out(Sum), .sel(Cin));
endmodule

module LOGIC_UNIT_4 (
  input  [3:0] A,
  input  [3:0] B,
  input  [1:0] f,
  output [3:0] Result
);

  wire [3:0] and_1_out, or_1_out, xor_1_out;

  assign and_1_out = A & B;  // AND_Gate and_1, 4 bits wide
  assign or_1_out = A | B;  // OR_Gate or_1, 4 bits wide
  assign xor_1_out = A ^ B;  // XOR_Gate xor_1, 4 bits wide
  Multiplexer #(.select(2), .width(4)) multiplexer_1 (
    .in0(and_1_out), .in1(or_1_out), .in2(xor_1_out), .in3(B), .out(Result), .sel(f));
endmodule

module ALU (
  input  [3:0] A,
  input  [3:0] B,
  input  [3:0] Opcode,
  output [3:0] out_4,
  output O,
  output C,
  output Z,
  output N
);

  wire [3:0] adder_4_1_sum, logic_unit_4_1_result;

  ADDER_4 adder_4_1 (.A(A), .B(B), .Cin(Opcode[0]), .Sum(adder_4_1_sum), .Overflow(O), .Carry(C));
  LOGIC_UNIT_4 logic_unit_4_1 (.A(A), .B(B), .f(Opcode[2:1]), .Result(logic_unit_4_1_result));
  Multiplexer #(.width(4)) multiplexer_1 (
    .in0(adder_4_1_sum), .in1(logic_unit_4_1_result), .out({N, out_4[2:0]}), .sel(Opcode[3]));
  nor nor_1 (Z, out_4[0], out_4[1], out_4[2], N);

  assign out_4[3] = N;
endmodule

module CPU (
  output [15:0] out_1,
  output [15:0] out_2,
  output [7:0] out_3,
  output Overflow,
  output Carry,
  output Zero,
  output Negative
);

  wire clk, Data, MoveImmd, or_1_out, or_2_out;
  wire [2:0] controlled_buffer_2_out;
  wire [3:0] alu_1_out_4, controlled_buffer_1_out, reg_file_1_out_a, reg_file_1_out_b;

  assign controlled_buffer_1_out = MoveImmd ? out_1[6:3] : 4'bz;  // Controlled_Buffer controlled_buffer_1
  Clock clock_1 (.out(clk));
  Counter counter_1 (.clr(1'b0), .load(1'b0), .up(1'b1), .count(1'b1), .clk(clk), .Q(out_3));  // open: D, carry
  or or_1 (or_1_out, Data, MoveImmd);
  assign controlled_buffer_2_out = or_2_out ? out_1[2:0] : 3'bz;  // Controlled_Buffer controlled_buffer_2
  or or_2 (or_2_out, Data, MoveImmd);
  assign controlled_buffer_1_out = Data ? alu_1_out_4 : 4'bz;  // Controlled_Buffer controlled_buffer_3
  ROM #(.dataWidth(16)) rom_1 (.addr(out_3), .data(out_2));
  REG_FILE reg_file_1 (
    .CLK(clk), .Write(or_1_out), .IN_VAL(controlled_buffer_1_out), .Ra(out_1[8:6]),
    .Rd(controlled_buffer_2_out), .Rb(out_1[5:3]), .OUT_A(reg_file_1_out_a), .OUT_B(reg_file_1_out_b));
  Register #(.width(16)) Inst_REG (.D(out_2), .en(1'b1), .clk(clk), .Q(out_1));  // open: clr
  and and_1 (Data, ~out_1[15], ~out_1[14], out_1[13]);  // AND_Gate
  and and_2 (MoveImmd, ~out_1[15], out_1[14], out_1[13]);  // AND_Gate
  ALU alu_1 (
    .A(reg_file_1_out_a), .B(reg_file_1_out_b), .Opcode(out_1[12:9]), .out_4(alu_1_out_4), .O(Overflow),
    .C(Carry), .Z(Zero), .N(Negative));

  // Other names for the same wires on the sheet: op[3:0] = out_1[12:9]; Ra[2:0] = out_1[8:6]; Rd[2:0] = out_1[2:0];
  //   Rb[2:0] = out_1[5:3]; value[3:0] = out_1[6:3]

  // Notes on the sheet:
  //   contents of rom_1 (hex, n*v repeats v):
  //   6019 6012 2056 0 2256
endmodule

module REG_FILE (
  input  CLK,
  input  Write,
  input  [3:0] IN_VAL,
  input  [2:0] Ra,
  input  [2:0] Rd,
  input  [2:0] Rb,
  output [3:0] OUT_A,
  output [3:0] OUT_B
);

  wire demultiplexer_1_out0, demultiplexer_1_out1, demultiplexer_1_out2, demultiplexer_1_out3,
       demultiplexer_1_out4, demultiplexer_1_out5, demultiplexer_1_out6, demultiplexer_1_out7;
  wire [3:0] R0_q, R1_q, R2_q, R3_q, R4_q, R5_q, R6_q, R7_q;

  Demultiplexer #(.select(3)) demultiplexer_1 (
    .out0(demultiplexer_1_out0), .out1(demultiplexer_1_out1), .out2(demultiplexer_1_out2),
    .out3(demultiplexer_1_out3), .out4(demultiplexer_1_out4), .out5(demultiplexer_1_out5),
    .out6(demultiplexer_1_out6), .out7(demultiplexer_1_out7), .in(Write), .sel(Rd));
  Register #(.width(4)) R0 (.D(IN_VAL), .en(demultiplexer_1_out0), .clk(CLK), .Q(R0_q), .clr(1'b0));
  Register #(.width(4)) R1 (.D(IN_VAL), .en(demultiplexer_1_out1), .clk(CLK), .Q(R1_q));  // open: clr
  Register #(.width(4)) R2 (.D(IN_VAL), .en(demultiplexer_1_out2), .clk(CLK), .Q(R2_q));  // open: clr
  Register #(.width(4)) R3 (.D(IN_VAL), .en(demultiplexer_1_out3), .clk(CLK), .Q(R3_q));  // open: clr
  Register #(.width(4)) R4 (.D(IN_VAL), .en(demultiplexer_1_out4), .clk(CLK), .Q(R4_q));  // open: clr
  Register #(.width(4)) R5 (.D(IN_VAL), .en(demultiplexer_1_out5), .clk(CLK), .Q(R5_q));  // open: clr
  Register #(.width(4)) R6 (.D(IN_VAL), .en(demultiplexer_1_out6), .clk(CLK), .Q(R6_q));  // open: clr
  Register #(.width(4)) R7 (.D(IN_VAL), .en(demultiplexer_1_out7), .clk(CLK), .Q(R7_q));  // open: clr
  Multiplexer #(.select(3), .width(4)) multiplexer_1 (
    .in0(R0_q), .in1(R1_q), .in2(R2_q), .in3(R3_q), .in4(R4_q), .in5(R5_q), .in6(R6_q), .in7(R7_q),
    .out(OUT_A), .sel(Ra));
  Multiplexer #(.select(3), .width(4)) multiplexer_2 (
    .in0(R0_q), .in1(R1_q), .in2(R2_q), .in3(R3_q), .in4(R4_q), .in5(R5_q), .in6(R6_q), .in7(R7_q),
    .out(OUT_B), .sel(Rb));
endmodule

module CPU2 (
  output [15:0] out_1,
  output [15:0] out_2,
  output [7:0] out_3,
  output Overflow,
  output Carry,
  output Zero,
  output Negative
);

  wire clk, Data, Load, MoveImmd, not_1_out, or_1_out, or_2_out, Store;
  wire [2:0] controlled_buffer_4_out, controlled_buffer_6_out;
  wire [3:0] alu2_1_out_4, controlled_buffer_1_out, controlled_buffer_2_out, ram_1_dout, reg_file_1_out_a,
       StoreData;

  assign controlled_buffer_1_out = Store ? StoreData : 4'bz;  // Controlled_Buffer controlled_buffer_1
  RAM #(.addrWidth(10), .dataWidth(4), .enables("line")) ram_1 (
    .addr(out_1[12:3]), .we(Store), .clk(clk), .din(controlled_buffer_1_out), .dout(ram_1_dout));
  Counter counter_1 (.clr(1'b0), .load(1'b0), .up(1'b1), .count(1'b1), .clk(clk), .Q(out_3));  // open: D, carry
  assign controlled_buffer_2_out = MoveImmd ? out_1[6:3] : 4'bz;  // Controlled_Buffer controlled_buffer_2
  Clock clock_1 (.out(clk));
  assign controlled_buffer_2_out = Load ? ram_1_dout : 4'bz;  // Controlled_Buffer controlled_buffer_3
  assign controlled_buffer_4_out = or_1_out ? out_1[2:0] : 3'bz;  // Controlled_Buffer controlled_buffer_4
  or or_1 (or_1_out, Data, Load, MoveImmd, Store);
  or or_2 (or_2_out, Data, Load, MoveImmd);
  ROM #(.dataWidth(16)) rom_1 (.addr(out_3), .data(out_2));
  assign controlled_buffer_2_out = Data ? alu2_1_out_4 : 4'bz;  // Controlled_Buffer controlled_buffer_5
  assign controlled_buffer_6_out = Store ? controlled_buffer_4_out : 3'bz;  // Controlled_Buffer controlled_buffer_6
  assign controlled_buffer_6_out = not_1_out ? out_1[5:3] : 3'bz;  // Controlled_Buffer controlled_buffer_7
  not not_1 (not_1_out, Store);
  Register #(.width(16)) Inst_REG (.D(out_2), .en(1'b1), .clk(clk), .Q(out_1));  // open: clr
  REG_FILE reg_file_1 (
    .CLK(clk), .Write(or_2_out), .IN_VAL(controlled_buffer_2_out), .Ra(out_1[8:6]),
    .Rd(controlled_buffer_4_out), .Rb(controlled_buffer_6_out), .OUT_A(reg_file_1_out_a), .OUT_B(StoreData));
  and and_1 (Data, ~out_1[15], ~out_1[14], out_1[13]);  // AND_Gate
  and and_2 (MoveImmd, ~out_1[15], out_1[14], out_1[13]);  // AND_Gate
  and and_3 (Store, ~out_1[15], out_1[14], ~out_1[13]);  // AND_Gate
  and and_4 (Load, out_1[15], ~out_1[14], ~out_1[13]);  // AND_Gate
  alu2 alu2_1 (
    .A(reg_file_1_out_a), .B(StoreData), .Opcode(out_1[12:9]), .out_4(alu2_1_out_4), .O(Overflow), .C(Carry),
    .Z(Zero), .N(Negative));

  // Other names for the same wires on the sheet: addr[9:0] = out_1[12:3]; Rb[2:0] = out_1[5:3];
  //   value[3:0] = out_1[6:3]; Ra[2:0] = out_1[8:6]; op[3:0] = out_1[12:9]; Rd[2:0] = out_1[2:0]

  // Notes on the sheet:
  //   contents of rom_1 (hex, n*v repeats v):
  //   6019 6012 2056 4039 2253 0 803c 0 0 3c27
  //   Move 3 to [R1]
  //   Move 2 to [R2]
  //   Add [R1]+[R2]-> [R6]
  //   Store [7] of RAM from [R1]
  //   Sub [R1]-[R2]-> [R3]
  //   Load [7] of RAM to [R4]
  //   001 Data
  //   011 Move
  //   010 Store
  //   100 Load
  //   0000 Add
  //   0001 Sub
  //   1000 and
  //   1010 or
  //   1100 xor
  //   011 00 [8bit number] [Rd]
  //   010 [10 bit addr] [Rd]
  //   100 [10 bit addr] [Rd]
  //   001xxxx[R1][R2][Rd]
  //   0110 0000 0001 1001
  //   0110 0000 0001 0010
  //   0010 0000 0101 0110
  //   0100 0000 0011 1001
  //   0010 0010 0101 0011
  //   1000 0000 0011 1100
  //   001 1110 000 100 111
  //   6019
  //   6012
  //   2056
  //   4039
  //   2253
  //   803c
endmodule

module addersub (
  input  Cin,
  input  [3:0] A,
  input  [3:0] B,
  output [3:0] Sum,
  output Overflow,
  output Carry
);

  wire adder_1_cout, adder_2_cout, adder_3_cout, xor_1_out, xor_2_out, xor_3_out, xor_4_out;

  xor xor_1 (xor_1_out, Cin, B[0]);
  xor xor_2 (xor_2_out, Cin, B[1]);
  xor xor_3 (xor_3_out, Cin, B[2]);
  xor xor_4 (xor_4_out, Cin, B[3]);
  Adder #(.width(1)) adder_1 (.a(A[0]), .b(xor_1_out), .out(Sum[0]), .cin(Cin), .cout(adder_1_cout));
  Adder #(.width(1)) adder_2 (.a(A[1]), .b(xor_2_out), .out(Sum[1]), .cin(adder_1_cout), .cout(adder_2_cout));
  Adder #(.width(1)) adder_3 (.a(A[2]), .b(xor_3_out), .out(Sum[2]), .cin(adder_2_cout), .cout(adder_3_cout));
  Adder #(.width(1)) adder_4 (.a(A[3]), .b(xor_4_out), .out(Sum[3]), .cin(adder_3_cout), .cout(Carry));
  xor xor_5 (Overflow, adder_3_cout, Carry);
endmodule

module alu2 (
  input  [3:0] A,
  input  [3:0] B,
  input  [3:0] Opcode,
  output [3:0] out_4,
  output O,
  output C,
  output Z,
  output N
);

  wire [3:0] addersub_1_sum, logic_unit_4_1_result;

  LOGIC_UNIT_4 logic_unit_4_1 (.A(A), .B(B), .f(Opcode[2:1]), .Result(logic_unit_4_1_result));
  addersub addersub_1 (.Cin(Opcode[0]), .A(A), .B(B), .Sum(addersub_1_sum), .Overflow(C), .Carry(O));
  Multiplexer #(.width(4)) multiplexer_1 (
    .in0(addersub_1_sum), .in1(logic_unit_4_1_result), .out({N, out_4[2:0]}), .sel(Opcode[3]));
  nor nor_1 (Z, out_4[0], out_4[1], out_4[2], N);

  assign out_4[3] = N;
endmodule

module cputrial (
  output [15:0] out_1,
  output [15:0] out_2,
  output [7:0] out_3,
  output Overflow,
  output Carry,
  output Zero,
  output Negative
);

  wire clk, Data, MoveImmd, or_1_out, or_2_out;
  wire [2:0] controlled_buffer_2_out;
  wire [3:0] alu2_1_out_4, controlled_buffer_1_out, reg_file_1_out_a, reg_file_1_out_b;

  assign controlled_buffer_1_out = MoveImmd ? out_1[6:3] : 4'bz;  // Controlled_Buffer controlled_buffer_1
  Clock clock_1 (.out(clk));
  Counter counter_1 (.clr(1'b0), .load(1'b0), .up(1'b1), .count(1'b1), .clk(clk), .Q(out_3));  // open: D, carry
  or or_1 (or_1_out, Data, MoveImmd);
  assign controlled_buffer_2_out = or_2_out ? out_1[2:0] : 3'bz;  // Controlled_Buffer controlled_buffer_2
  or or_2 (or_2_out, Data, MoveImmd);
  assign controlled_buffer_1_out = Data ? alu2_1_out_4 : 4'bz;  // Controlled_Buffer controlled_buffer_3
  ROM #(.dataWidth(16)) rom_1 (.addr(out_3), .data(out_2));
  REG_FILE reg_file_1 (
    .CLK(clk), .Write(or_1_out), .IN_VAL(controlled_buffer_1_out), .Ra(out_1[8:6]),
    .Rd(controlled_buffer_2_out), .Rb(out_1[5:3]), .OUT_A(reg_file_1_out_a), .OUT_B(reg_file_1_out_b));
  Register #(.width(16)) Inst_REG (.D(out_2), .en(1'b1), .clk(clk), .Q(out_1));  // open: clr
  and and_1 (Data, ~out_1[15], ~out_1[14], out_1[13]);  // AND_Gate
  and and_2 (MoveImmd, ~out_1[15], out_1[14], out_1[13]);  // AND_Gate
  alu2 alu2_1 (
    .A(reg_file_1_out_a), .B(reg_file_1_out_b), .Opcode(out_1[12:9]), .out_4(alu2_1_out_4), .O(Overflow),
    .C(Carry), .Z(Zero), .N(Negative));

  // Other names for the same wires on the sheet: op[3:0] = out_1[12:9]; Ra[2:0] = out_1[8:6]; Rd[2:0] = out_1[2:0];
  //   Rb[2:0] = out_1[5:3]; value[3:0] = out_1[6:3]

  // Notes on the sheet:
  //   contents of rom_1 (hex, n*v repeats v):
  //   6019 6012 2056 0 2257
  //   001 Data
  //   011 Move
  //   0000 Add
  //   0001 Sub
  //   1000 and
  //   1010 or
  //   1100 xor
endmodule
